# Fritzing sketch mstation (saved by Fritzing 0.9.0b)
stripboards: 3

parts:
  LCD1 = LCD screen
  DHT1 = DHT11 Humitidy and Temperature Sensor
  R1 = Resistor [tolerance=±5% resistance=4.7k package=THT]
  DS1 = DS18B20 1-Wire Temperature Sensor [part_number=DS18B20]
  R2 = Resistor [tolerance=±5% resistance=4.7k package=THT]
  Часть1 = Arduino Uno (Rev3) - ICSP

nets:
  GND: LCD1.VSS, LCD1.V0, LCD1.R/W, LCD1.LED-, DHT1.GND, DS1.GND, Часть1.GND
  VDD: LCD1.VDD, LCD1.LED+, DHT1.VDD, R1.Pin_1, DS1.VDD, R2.Pin_1, Часть1.5V
  N1: LCD1.RS, Часть1.D4
  N2: LCD1.E, Часть1.D5_PWM
  N3: LCD1.DB4, Часть1.D8
  N4: LCD1.DB5, Часть1.D9_PWM
  N5: LCD1.DB6, Часть1.D10_PWM/SS
  N6: LCD1.DB7, Часть1.ICSP_MOSI, Часть1.D11_PWM/MOSI
  N7: DHT1.DATA, R1.Pin_0, Часть1.D2
  N8: DS1.DQ, R2.Pin_0, Часть1.D3_PWM

custom parts:
  DHT11 Humitidy and Temperature Sensor: DHT11 Humidity and Temperature Sensor
